# Fritzing sketch Layout (saved by Fritzing 0.9.4)
breadboards: 1

parts:
  WeMos_D1_Mini1 = WeMos D1 Mini
  HC-SR04_Sensor_1 = HC-SR04 Ultrasonic Distance Sensor
  LED1 = LED - 3mm [color="Red (633nm)" package="3 mm [THT]"]
  J1 = Piezo Speaker
  R1 = Resistor [tolerance=±5% resistance=220 package="0603 [SMD]"]
  Q1 = NPN-Transistor [package="SOT-23 [SMD]"]
  R2 = Resistor [tolerance=±5% resistance=1k package=THT]  # not connected
  VCC1 = 4 x AAA Battery Mount

nets:
  5V: WeMos_D1_Mini1.5V, HC-SR04_Sensor_1.VCC, J1.pin2, VCC1.+
  N1: WeMos_D1_Mini1.D1, R1.Pin_1
  N2: WeMos_D1_Mini1.D6, HC-SR04_Sensor_1.ECHO
  N3: WeMos_D1_Mini1.D7, HC-SR04_Sensor_1.TRIG
  N4: WeMos_D1_Mini1.G, HC-SR04_Sensor_1.GND, LED1.cathode, Q1.2, VCC1.-
  N5: LED1.anode, R1.Pin_0
  N6: J1.pin1, Q1.1
